# Fritzing sketch fritzing (saved by Fritzing 0.9.6b)
breadboards: 1

parts:
  U1 = NodeMCU V3.0
  LED1 = LEDs [package=led10mm]
  LED2 = LEDs [package=led10mm]
  Q1 = TRANSISTOR_NPN [package=to-92]

nets:
  N1: U1.D2, Q1.B
  N2: U1.3V3, LED1.A, LED2.A
  N3: U1.GND#6, U1.GND#13, U1.GND#16, U1.GND#33, Q1.E
  N4: LED1.C, LED2.C, Q1.C

custom parts:
  NodeMCU V3.0: ESP8266 based NodeMCU
